# Fritzing sketch ir (saved by Fritzing 0.9.4)
circuit board: 2.12251cm x 4.05494cm
breadboards: 1

parts:
  C1 = Ceramic Capacitor [capacitance=0.1µF package="1206 [SMD, multilayer]"]
  C2 = Capacitor Polarized [part_number=1000μF package=panasonic_h13]
  U1 = ESP8266 WiFi Module [part_number=ESP8266]
  R6 = Resistor [tolerance=±5% resistance=4.7k package=THT]
  R7 = Resistor [tolerance=±5% resistance=10k package=THT]
  2n3904 = NPN-Transistor [package="TO92 [THT]"]
  IR = TSOP312.., 314.. [package=THT]
  LED = LED - 3mm [color="Infrared (850nm)" package="3 mm [THT]"]
  NightLight = USB Connectors [package=usb-microb]
  PIR1 = PIR sensor
  DS1 = DS18B20 1-Wire Temperature Sensor [part_number=DS18B20]
  IC1 = V_REG_LD1117VXX [package=78xxl]
  Power = USB Connectors [package=usb-microb]
  R5 = Resistor [tolerance=±5% resistance=4.7k package=THT]
  R8 = Resistor [tolerance=±5% resistance=100 package=THT]
  R9 = Resistor [tolerance=±5% resistance=100 package=THT]
  C3 = Ceramic Capacitor [capacitance=0.1µF package="1206 [SMD, multilayer]"]

nets:
  GND: C1.0, C2.-, U1.GND, 2n3904.E, IR.GND, NightLight.GND, PIR1.GND, DS1.GND, IC1.GND, Power.GND, C3.0
  3.3V: C1.1, C2.+, U1.VCC, U1.CH_PD, U1.REST, R7.Pin_0, DS1.VDD, IC1.OUT, R5.Pin_0, R8.Pin_0, R9.Pin_0
  N1: U1.GPIO_0, R7.Pin_1
  N2: U1.GPIO_5, NightLight.D+
  N3: U1.GPIO_16, PIR1.SIG
  N4: U1.GPIO_14, IR.Data
  N5: U1.GPIO_12, DS1.DQ, R5.Pin_1
  N6: U1.GPIO_13, R6.Pin_0
  N7: R6.Pin_1, 2n3904.B
  N8: 2n3904.C, LED.cathode
  N9: IR.Vs, R9.Pin_1, C3.1
  N10: LED.anode, R8.Pin_1
  5V: NightLight.VBUS, PIR1.VDD, IC1.IN, Power.VBUS

custom parts:
  ESP8266 WiFi Module: Generic WiFi Module based on the ESP8266 with onboard PCB antenna and UART communications
